# Fritzing sketch NeptuneBox Schematic (saved by Fritzing 0.9.3b)
circuit board: 12.2661cm x 8.45338cm
breadboards: 1

parts:
  Arduino_Due = Arduino Due (Rev2b)
  ESP-07 = ESP8266 WiFi Module [part_number=ESP8266]
  CAN_Transceiver = MCP2551 [package=so08]
  NMEA_2000_Bus_Data = Screw terminal - 2 pins [package=THT]

nets:
  N1: Arduino_Due.CANRX, CAN_Transceiver.RXD
  N2: Arduino_Due.CANTX, CAN_Transceiver.TXD
  N3: Arduino_Due.D18/TX1, ESP-07.RXD
  N4: Arduino_Due.D19/RX1, ESP-07.TXD
  VCC: Arduino_Due.IOREF, ESP-07.VCC, ESP-07.CH_PD, CAN_Transceiver.VDD
  GND: Arduino_Due.GND, ESP-07.GND, ESP-07.GPIO_15, CAN_Transceiver.VSS
  12V: Arduino_Due.VIN
  N5: CAN_Transceiver.CANL, NMEA_2000_Bus_Data.pin2
  N6: CAN_Transceiver.CANH, NMEA_2000_Bus_Data.pin1

notes:
  NeptuneBox, Ryan Maxfield - ryan.maxfield@neptunebox.com, 03
